// Logisim project GUESS_THE_NUMBER_XTREME.circ as structural Verilog: 8 circuits, main circuit main
module main (
  input  in_1,
  input  in_2,
  input  in_3,
  input  in_4,
  input  in_5,
  input  in_6,
  input  in_7,
  input  in_8,
  input  in_9,
  input  in_10
);

  wire A_DEAD, A_JOGANDO, A_VENCEU, ACERTOU, and_6_out, and_7_out, and_8_out, and_9_out, AW, AW_2, B_DEAD,
       B_JOGANDO, B_VENCEU, BW, BW_2, CHUTANDO_X, CHUTANDO_Y, CHUTAR, clock_1_out, comparador_1_a___b,
       comparador_1_a___b_2, comparador_1_iguais, CONFIGURAR, CONFIRMAR, d_ff_1_qn, d_ff_2_qn,
       demultiplexer_1_out0, demultiplexer_1_out1, dma_t, dmb_t, dmx_t, dsa_t, dsb_t, dsx_t, EMPATE,
       FIM_DE_JOGO, GERAR, GLOBAL_CLOCK, IGUAL, MAIOR, MENOR, not_1_out, or_4_out, \PRÓXIMO , RESET, SA, SB,
       START, START_G, SX, SY, tunnel, TURNOUT, uma_t, umb_t, umx_t, usa_t, usb_t, usx_t;
  wire [3:0] CHUTE_A, CHUTE_B, core_1_xh, core_1_yh, DMA, DMB, DMX, DSA, DSB, DSX, GA, GB, PA, PB, UMA, UMB,
       UMX, USA, USB, USX, XH, YH;

  TRECO_NUMERO treco_numero_1 (
    .I3(in_1), .E3(GA[3]), .I2(in_2), .I1(in_3), .I0(in_4), .E2(GA[2]), .E1(GA[1]), .E0(GA[0]),
    .S3(CHUTE_A[3]), .S2(CHUTE_A[2]), .S1(CHUTE_A[1]), .S0(CHUTE_A[0]), .SINAL(SA));
  TRECO_NUMERO treco_numero_2 (
    .I3(in_5), .E3(GB[3]), .I2(in_6), .I1(in_7), .I0(in_8), .E2(GB[2]), .E1(GB[1]), .E0(GB[0]),
    .S3(CHUTE_B[3]), .S2(CHUTE_B[2]), .S1(CHUTE_B[1]), .S0(CHUTE_B[0]), .SINAL(SB));
  D_Flip_Flop d_ff_1 (.clk(START), .D(d_ff_1_qn), .Q(START_G), .Qn(d_ff_1_qn));  // open: preset, en, reset
  Button button_1 (.out(dma_t));
  Button button_2 (.out(uma_t));
  Hex_Digit_Display hex_digit_display_1 (.value(DMA));  // open: dp
  Hex_Digit_Display hex_digit_display_2 (.value(UMA));  // open: dp
  LED led_1 (.in(SA));
  and and_1 (A_JOGANDO, START_G, ~TURNOUT);  // AND_Gate
  Hex_Digit_Display hex_digit_display_3 (.value(PA));  // open: dp
  Button button_3 (.out(dsa_t));
  LED led_2 (.in(1'b1));
  LED led_3 (.in(1'b1));
  Hex_Digit_Display hex_digit_display_4 (.value(DSA));  // open: dp
  Hex_Digit_Display hex_digit_display_5 (.value(GA));  // open: dp
  LED led_4 (.in(A_JOGANDO));
  and and_2 (B_JOGANDO, START_G, TURNOUT);
  Button button_4 (.out(usa_t));
  Hex_Digit_Display hex_digit_display_6 (.value(USA));  // open: dp
  D_Flip_Flop d_ff_2 (.clk(CONFIGURAR), .D(d_ff_2_qn), .Q(tunnel), .Qn(d_ff_2_qn));  // open: preset, en, reset
  LED led_5 (.in(A_VENCEU));
  Button button_5 (.out(START));
  LED led_6 (.in(MAIOR));
  Button button_6 (.out(\PRÓXIMO ));
  LED led_7 (.in(SX));
  Hex_Digit_Display hex_digit_display_7 (.value(XH));  // open: dp
  LED led_8 (.in(CHUTANDO_X));
  \Cronômetro  \cronômetro_1  (
    .RESET(RESET), .CLK(GLOBAL_CLOCK), .DM(DMX), .UM(UMX), .DS(DSX), .US(USX), .MODE(tunnel),
    .out_11(A_DEAD), .START(START_G), .PAUSE_X(TURNOUT), .DM_EXIT(DMA), .UM_EXIT(UMA), .DS_EXIT(DSA),
    .US_EXIT(USA), .CONFIRMAR(CONFIRMAR));
  LED led_9 (.in(FIM_DE_JOGO));
  LED led_10 (.in(EMPATE));
  LED led_11 (.in(tunnel));
  Button button_7 (.out(CONFIGURAR));
  LED led_12 (.in(ACERTOU));
  LED led_13 (.in(IGUAL));
  Button button_8 (.out(CHUTAR));
  Demultiplexer demultiplexer_1 (
    .out0(demultiplexer_1_out0), .out1(demultiplexer_1_out1), .in(ACERTOU), .sel(TURNOUT));  // open: en
  LED led_14 (.in(B_VENCEU));
  Button button_9 (.out(CONFIRMAR));
  LED led_15 (.in(MENOR));
  Button button_10 (.out(GERAR));
  LED led_16 (.in(SY));
  Hex_Digit_Display hex_digit_display_8 (.value(YH));  // open: dp
  LED led_17 (.in(CHUTANDO_Y));
  Counter #(.width(4), .max('hf)) counter_1 (.Q(PA), .clk(demultiplexer_1_out0));  // open: load, D, count, carry, clr
  Counter #(.width(4), .max('hf)) counter_2 (.Q(PB), .clk(demultiplexer_1_out1));  // open: load, D, count, carry, clr
  Button button_11 (.out(RESET));
  Button button_12 (.out(umb_t));
  Button button_13 (.out(dmb_t));
  Hex_Digit_Display hex_digit_display_9 (.value(UMB));  // open: dp
  Hex_Digit_Display hex_digit_display_10 (.value(DMB));  // open: dp
  LED led_18 (.in(SB));
  Hex_Digit_Display hex_digit_display_11 (.value(PB));  // open: dp
  Button button_14 (.out(dsb_t));
  LED led_19 (.in(1'b1));
  LED led_20 (.in(1'b1));
  Hex_Digit_Display hex_digit_display_12 (.value(DSB));  // open: dp
  Hex_Digit_Display hex_digit_display_13 (.value(GB));  // open: dp
  LED led_21 (.in(B_JOGANDO));
  or or_1 (A_VENCEU, AW, AW_2);
  or or_2 (B_VENCEU, BW, BW_2);
  or or_3 (FIM_DE_JOGO, A_VENCEU, EMPATE, B_VENCEU);
  TRECO_NUMERODOIS treco_numerodois_1 (
    .I3(core_1_xh[3]), .I2(core_1_xh[2]), .I1(core_1_xh[1]), .I0(core_1_xh[0]), .E3(XH[3]), .E2(XH[2]),
    .E1(XH[1]), .E0(XH[0]), .SINAL(SX));
  Core core_1 (
    .CHUTE_A(CHUTE_A), .CHUTE_B(CHUTE_B), .A_DEAD(A_DEAD), .B_DEAD(B_DEAD), .\PRÓXIMO (\PRÓXIMO ),
    .CHUTAR(CHUTAR), .RESET(RESET), .TURNOUT(TURNOUT), .AGUARDANDO_X(CHUTANDO_X), .AGUARDANDO_Y(CHUTANDO_Y),
    .MAIOR(MAIOR), .IGUAL(IGUAL), .MENOR(MENOR), .XH(core_1_xh), .YH(core_1_yh), .ACERTOU(ACERTOU),
    .START(START_G), .macria(GERAR));  // open: RESULTADO_DO_CHUTE
  TRECO_NUMERODOIS treco_numerodois_2 (
    .I3(core_1_yh[3]), .I2(core_1_yh[2]), .I1(core_1_yh[1]), .I0(core_1_yh[0]), .E3(YH[3]), .E2(YH[2]),
    .E1(YH[1]), .E0(YH[0]), .SINAL(SY));
  \Cronômetro  \cronômetro_2  (
    .RESET(RESET), .CLK(GLOBAL_CLOCK), .DM(DMX), .UM(UMX), .DS(DSX), .US(USX), .MODE(tunnel),
    .out_11(B_DEAD), .START(START_G), .PAUSE_X(not_1_out), .DM_EXIT(DMB), .UM_EXIT(UMB), .DS_EXIT(DSB),
    .US_EXIT(USB), .CONFIRMAR(CONFIRMAR));
  Button button_15 (.out(usb_t));
  Hex_Digit_Display hex_digit_display_14 (.value(USB));  // open: dp
  not not_1 (not_1_out, TURNOUT);
  Comparador comparador_1 (
    .A(PA), .B(PB), .IGUAIS(comparador_1_iguais), .A___B(comparador_1_a___b), .A___B_2(comparador_1_a___b_2));
  or or_4 (or_4_out, A_DEAD, B_DEAD);
  and and_3 (EMPATE, or_4_out, comparador_1_iguais);
  and and_4 (AW_2, comparador_1_a___b, or_4_out);
  and and_5 (BW_2, comparador_1_a___b_2, or_4_out);
  or or_5 (dmx_t, dma_t, dmb_t);
  or or_6 (umx_t, uma_t, umb_t);
  or or_7 (dsx_t, dsa_t, dsb_t);
  or or_8 (usx_t, usa_t, usb_t);
  and and_6 (and_6_out, dmx_t, tunnel);
  and and_7 (and_7_out, umx_t, tunnel);
  and and_8 (and_8_out, dsx_t, tunnel);
  and and_9 (and_9_out, usx_t, tunnel);
  Clock clock_1 (.out(clock_1_out));
  Comparador comparador_2 (.A(PA), .B(4'b1111), .IGUAIS(AW));  // open: A___B, A___B_2
  Comparador comparador_3 (.A(PB), .B(4'b1111), .IGUAIS(BW));  // open: A___B, A___B_2
  Counter #(.width(4), .max('h5)) counter_3 (
    .load(1'b1), .count(1'b1), .Q(DMX), .clk(and_6_out), .clr(RESET));  // open: D, carry
  Counter #(.width(4), .max('h9)) counter_4 (
    .load(1'b1), .count(1'b1), .Q(UMX), .clk(and_7_out), .clr(RESET));  // open: D, carry
  Counter #(.width(4), .max('h5)) counter_5 (
    .load(1'b1), .count(1'b1), .Q(DSX), .clk(and_8_out), .clr(RESET));  // open: D, carry
  Counter #(.width(4), .max('h9)) counter_6 (
    .load(1'b1), .count(1'b1), .Q(USX), .clk(and_9_out), .clr(RESET));  // open: D, carry
  and and_10 (GLOBAL_CLOCK, clock_1_out, ~FIM_DE_JOGO);  // AND_Gate

  // Other names for the same wires on the sheet: A0 = in_4; A1 = in_3; A2 = in_2; A3 = in_1; B0 = in_8; B1 = in_7;
  //   B2 = in_6; B3 = in_5; GERAR_NOVO_NUMERO = GERAR; PAUSE_A = in_9; PAUSE_B = in_10

  // Notes on the sheet:
  //   JOGADOR - A
  //   DADOS DO MODO DIFÍCIL
  //   JOGADOR - B
endmodule

module Comparador (
  input  [3:0] A,
  input  [3:0] B,
  output IGUAIS,
  output A___B,
  output A___B_2
);

  wire and_1_out, and_2_out, and_3_out, and_4_out, not_1_out, not_2_out, not_3_out, not_4_out, xnor_1_out,
       xnor_2_out, xnor_3_out, xnor_4_out;

  xnor xnor_1 (xnor_1_out, A[3], B[3]);
  xnor xnor_2 (xnor_2_out, A[2], B[2]);
  xnor xnor_3 (xnor_3_out, A[1], B[1]);
  xnor xnor_4 (xnor_4_out, A[0], B[0]);
  not not_1 (not_1_out, B[3]);
  not not_2 (not_2_out, B[2]);
  not not_3 (not_3_out, B[1]);
  not not_4 (not_4_out, B[0]);
  and and_1 (and_1_out, A[3], not_1_out);
  and and_2 (and_2_out, xnor_1_out, A[2], not_2_out);
  and and_3 (and_3_out, xnor_1_out, xnor_2_out, A[1], not_3_out);
  and and_4 (and_4_out, xnor_3_out, xnor_2_out, xnor_1_out, A[0], not_4_out);
  and and_5 (IGUAIS, xnor_1_out, xnor_2_out, xnor_3_out, xnor_4_out);
  or or_1 (A___B, and_1_out, and_2_out, and_3_out, and_4_out);
  nor nor_1 (A___B_2, IGUAIS, A___B);
endmodule

module \Cronômetro  (
  input  START,
  input  PAUSE_X,
  input  MODE,
  input  CONFIRMAR,
  input  CLK,
  input  RESET,
  input  [3:0] DM,
  input  [3:0] UM,
  input  [3:0] DS,
  input  [3:0] US,
  output out_11,
  output [3:0] DM_EXIT,
  output [3:0] UM_EXIT,
  output [3:0] DS_EXIT,
  output [3:0] US_EXIT
);

  wire and_1_out, and_2_out, and_3_out, and_4_out, and_7_out, and_9_out, and_10_out, and_11_out, CLOCK,
       DMX_MIN, DMX_minus, DSX_MIN, DSX_minus, not_1_out, not_2_out, not_3_out, not_4_out, not_5_out,
       or_1_out, or_2_out, or_3_out, or_4_out, or_5_out, or_6_out, or_7_out, or_8_out, UMX_MIN, UMX_minus,
       USX_MIN;
  wire [3:0] _0, _1, _2, _3;

  and and_1 (and_1_out, PAUSE_X, START);
  and and_2 (and_2_out, CLK, START, ~PAUSE_X);  // AND_Gate
  and and_3 (and_3_out, ~out_11, and_2_out);  // AND_Gate
  not not_1 (not_1_out, MODE);
  or or_1 (or_1_out, START, and_1_out);
  not not_2 (not_2_out, or_2_out);
  or or_2 (or_2_out, DMX_minus, CONFIRMAR);
  Multiplexer multiplexer_1 (.in0(and_3_out), .in1(1'b0), .out(CLOCK), .sel(MODE));  // open: en
  Counter #(.width(4), .max('h5)) counter_1 (
    .load(not_1_out), .D(DM), .count(or_1_out), .Q(_3), .carry(DMX_MIN), .clk(not_2_out), .clr(RESET));
  and and_4 (and_4_out, PAUSE_X, START);
  Counter #(.width(4), .max('h9)) counter_2 (
    .load(not_1_out), .D(UM), .count(or_3_out), .Q(_2), .carry(UMX_MIN), .clk(not_3_out), .clr(RESET));
  or or_3 (or_3_out, START, and_4_out);
  not not_3 (not_3_out, or_4_out);
  or or_4 (or_4_out, UMX_minus, CONFIRMAR);
  and and_5 (out_11, DMX_MIN, UMX_MIN, DSX_MIN, USX_MIN);
  and and_6 (DMX_minus, START, UMX_MIN);
  and and_7 (and_7_out, PAUSE_X, START);
  or or_5 (or_5_out, START, and_7_out);
  not not_4 (not_4_out, or_6_out);
  or or_6 (or_6_out, DSX_minus, CONFIRMAR);
  Counter #(.width(4), .max('h5)) counter_3 (
    .load(not_1_out), .D(DS), .count(or_5_out), .Q(_1), .carry(DSX_MIN), .clk(not_4_out), .clr(RESET));
  and and_8 (UMX_minus, START, DSX_MIN);
  Multiplexer #(.width(4)) multiplexer_2 (.in0(DM), .in1(_3), .out(DM_EXIT), .sel(START));  // open: en
  Multiplexer #(.width(4)) multiplexer_3 (.in0(UM), .in1(_2), .out(UM_EXIT), .sel(START));  // open: en
  Multiplexer #(.width(4)) multiplexer_4 (.in0(DS), .in1(_1), .out(DS_EXIT), .sel(START));  // open: en
  Multiplexer #(.width(4)) multiplexer_5 (.in0(US), .in1(_0), .out(US_EXIT), .sel(START));  // open: en
  and and_9 (and_9_out, PAUSE_X, START);
  and and_10 (and_10_out, CLOCK, ~PAUSE_X);  // AND_Gate
  not not_5 (not_5_out, CONFIRMAR);
  and and_11 (and_11_out, not_5_out, ~START);  // AND_Gate
  Counter #(.width(4), .max('h9)) counter_4 (
    .load(not_1_out), .D(US), .count(or_7_out), .Q(_0), .carry(USX_MIN), .clk(or_8_out), .clr(RESET));
  or or_7 (or_7_out, START, and_9_out);
  or or_8 (or_8_out, and_10_out, and_11_out);
  and and_12 (DSX_minus, START, USX_MIN);

  // Other names for the same wires on the sheet: CONFIG = MODE; CONFIRMA = CONFIRMAR; DMX[3:0] = DM; DSX[3:0] = DS;
  //   END = out_11; PAUSE = PAUSE_X; S0[3:0] = US_EXIT; S1[3:0] = DS_EXIT; S2[3:0] = UM_EXIT; S3[3:0] = DM_EXIT;
  //   SUB_OK = START; UMX[3:0] = UM; USX[3:0] = US
endmodule

module Core (
  input  [3:0] CHUTE_A,
  input  [3:0] CHUTE_B,
  input  A_DEAD,
  input  B_DEAD,
  input  \PRÓXIMO ,
  input  CHUTAR,
  input  RESET,
  input  START,
  input  macria,
  output TURNOUT,
  output AGUARDANDO_X,
  output AGUARDANDO_Y,
  output RESULTADO_DO_CHUTE,
  output [3:0] XH,
  output [3:0] YH,
  output ACERTOU,
  output MAIOR,
  output IGUAL,
  output MENOR
);

  wire ACERTOU_t, and_1_out, comparator_1_eq, comparator_2_eq, IGUAL_t, MAIOR_t, MENOR_t, not_1_out,
       perry_o_ornitorrinco_1_chutando_x, perry_o_ornitorrinco_1_chutando_y,
       perry_o_ornitorrinco_1_exibindo_chute, perry_o_ornitorrinco_1_jogador;
  wire [3:0] RNG_X, RNG_Y;
  wire [4:0] adder_1_out, adder_2_out, C_X5, C_Y5, RNG_X5, RNG_Y5;

  and and_1 (and_1_out, \PRÓXIMO , START);
  and and_2 (TURNOUT, START, perry_o_ornitorrinco_1_jogador);
  Perry_o_Ornitorrinco perry_o_ornitorrinco_1 (
    .CLOCK(and_1_out), .JOGADOR(perry_o_ornitorrinco_1_jogador),
    .CHUTANDO_X(perry_o_ornitorrinco_1_chutando_x), .CHUTANDO_Y(perry_o_ornitorrinco_1_chutando_y),
    .EXIBINDO_CHUTE(perry_o_ornitorrinco_1_exibindo_chute));  // open: GERAR
  and and_3 (RESULTADO_DO_CHUTE, perry_o_ornitorrinco_1_exibindo_chute, START);
  and and_4 (AGUARDANDO_X, START, perry_o_ornitorrinco_1_chutando_x);
  and and_5 (AGUARDANDO_Y, perry_o_ornitorrinco_1_chutando_y, START);
  not not_1 (not_1_out, macria);
  Adder #(.width(5)) adder_1 (.a(C_X5), .b(C_Y5), .out(adder_1_out));  // open: cin, cout
  Adder #(.width(5)) adder_2 (.a(RNG_X5), .b(RNG_Y5), .out(adder_2_out));  // open: cin, cout
  Comparator #(.width(4)) comparator_1 (.a(YH), .b(RNG_Y), .eq(comparator_1_eq));  // open: gt, lt
  Comparator #(.width(4)) comparator_2 (.a(XH), .b(RNG_X), .eq(comparator_2_eq));  // open: gt, lt
  Random #(.width(4), .seed(13121989)) random_1 (.clk(not_1_out), .out(RNG_X));  // open: next, clr
  Random #(.width(4), .seed(4091981)) random_2 (.clk(not_1_out), .out(RNG_Y));  // open: next, clr
  Comparator #(.width(5)) comparator_3 (.a(adder_1_out), .b(adder_2_out), .gt(MAIOR_t), .eq(IGUAL_t), .lt(MENOR_t));
  and and_6 (MAIOR, MAIOR_t, RESULTADO_DO_CHUTE);
  and and_7 (ACERTOU_t, IGUAL_t, comparator_1_eq, comparator_2_eq);
  and and_8 (IGUAL, IGUAL_t, RESULTADO_DO_CHUTE);
  assign C_X5 = {{1{XH[3]}}, XH};  // Bit_Extender bit_extender_1
  assign C_Y5 = {{1{YH[3]}}, YH};  // Bit_Extender bit_extender_2
  assign RNG_X5 = {{1{RNG_X[3]}}, RNG_X};  // Bit_Extender bit_extender_3
  assign RNG_Y5 = {{1{RNG_Y[3]}}, RNG_Y};  // Bit_Extender bit_extender_4
  and and_9 (MENOR, MENOR_t, RESULTADO_DO_CHUTE);
  chute_nas_canela_de_qm_reclamar chute_nas_canela_de_qm_reclamar_1 (
    .IN_A(CHUTE_A), .IN_B(CHUTE_B), .JOGADOR(TURNOUT), .\PRÓXIMO (AGUARDANDO_Y), .RESET(RESET),
    .CHUTAR(CHUTAR), .E_X(XH), .E_Y(YH), .ALLOW(START));
  and and_10 (ACERTOU, ACERTOU_t, RESULTADO_DO_CHUTE);

  // Other names for the same wires on the sheet: C_X[3:0] = XH; C_Y[3:0] = YH; CHUTE_X = AGUARDANDO_X;
  //   CHUTE_Y = AGUARDANDO_Y; EXIBE_CHUTE = RESULTADO_DO_CHUTE; GERAR = macria; JOGADOR = TURNOUT
endmodule

module TRECO_NUMERO (
  input  I3,
  input  I2,
  input  I1,
  input  I0,
  output E3,
  output E2,
  output E1,
  output E0,
  output S3,
  output S2,
  output S1,
  output S0,
  output SINAL
);

  wire and_1_out, and_2_out, and_3_out, and_4_out, and_5_out, and_6_out, and_7_out, not_1_out, not_2_out,
       not_3_out, not_4_out, not_5_out, not_6_out, not_7_out, not_8_out, not_9_out, not_10_out, not_11_out;

  not not_1 (not_1_out, I2);
  not not_2 (not_2_out, I1);
  not not_3 (not_3_out, I0);
  not not_4 (not_4_out, I3);
  and and_1 (and_1_out, not_4_out, I2);
  not not_5 (not_5_out, I1);
  and and_2 (and_2_out, I2, not_5_out, not_6_out);
  not not_6 (not_6_out, I0);
  not not_7 (not_7_out, I2);
  and and_3 (and_3_out, I3, not_7_out, I0);
  and and_4 (and_4_out, I3, not_8_out, I1);
  not not_8 (not_8_out, I2);
  not not_9 (not_9_out, I3);
  and and_5 (and_5_out, not_9_out, I1);
  and and_6 (and_6_out, I1, not_10_out);
  not not_10 (not_10_out, I0);
  and and_7 (and_7_out, I3, not_11_out, I0);
  not not_11 (not_11_out, I1);
  and and_8 (E3, I3, not_1_out, not_2_out, not_3_out);
  or or_1 (E2, and_1_out, and_2_out, and_3_out, and_4_out);
  or or_2 (E1, and_5_out, and_6_out, and_7_out);

  assign E0 = I0;
  assign S0 = I0;
  assign S1 = I1;
  assign S2 = I2;
  assign S3 = I3;
  assign SINAL = I3;
endmodule

module chute_nas_canela_de_qm_reclamar (
  input  [3:0] IN_A,
  input  [3:0] IN_B,
  input  JOGADOR,
  input  \PRÓXIMO ,
  input  RESET,
  input  CHUTAR,
  input  ALLOW,
  output [3:0] E_X,
  output [3:0] E_Y
);

  wire and_1_out, and_2_out, CHUTAR_t, not_1_out, not_2_out, or_1_out, or_2_out, R;
  wire [3:0] demultiplexer_1_out0, demultiplexer_1_out1, multiplexer_1_out;

  and and_1 (and_1_out, JOGADOR, ALLOW);
  and and_2 (and_2_out, \PRÓXIMO , ALLOW);
  and and_3 (R, ~ALLOW, RESET);  // AND_Gate
  and and_4 (CHUTAR_t, ALLOW, CHUTAR);
  Multiplexer #(.width(4)) multiplexer_1 (
    .in0(IN_A), .in1(IN_B), .out(multiplexer_1_out), .sel(and_1_out));  // open: en
  Demultiplexer #(.width(4)) demultiplexer_1 (
    .out0(demultiplexer_1_out0), .out1(demultiplexer_1_out1), .in(multiplexer_1_out), .sel(and_2_out));  // open: en
  or or_1 (or_1_out, demultiplexer_1_out1[3], demultiplexer_1_out1[2], demultiplexer_1_out1[1], demultiplexer_1_out1[0]);
  or or_2 (or_2_out, demultiplexer_1_out0[3], demultiplexer_1_out0[2], demultiplexer_1_out0[1], demultiplexer_1_out0[0]);
  Register #(.width(4)) register_1 (.D(demultiplexer_1_out0), .en(not_1_out), .Q(E_X), .clk(CHUTAR_t), .clr(R));
  not not_1 (not_1_out, or_1_out);
  Register #(.width(4)) register_2 (.D(demultiplexer_1_out1), .en(not_2_out), .Q(E_Y), .clk(CHUTAR_t), .clr(R));
  not not_2 (not_2_out, or_2_out);
endmodule

module Perry_o_Ornitorrinco (
  input  CLOCK,
  output JOGADOR,
  output CHUTANDO_X,
  output CHUTANDO_Y,
  output EXIBINDO_CHUTE,
  output GERAR
);

  wire [1:0] adder_1_out, d_ff_2_q;

  D_Flip_Flop d_ff_1 (.clk(CLOCK), .D(adder_1_out[1]), .Q(d_ff_2_q[1]));  // open: Qn, preset, en, reset
  D_Flip_Flop d_ff_2 (.clk(CLOCK), .D(adder_1_out[0]), .Q(d_ff_2_q[0]));  // open: Qn, preset, en, reset
  Adder #(.width(2)) adder_1 (.a(d_ff_2_q), .b(2'b01), .out(adder_1_out));  // open: cin, cout
  and and_1 (CHUTANDO_X, adder_1_out[0], ~adder_1_out[1]);  // AND_Gate
  and and_2 (CHUTANDO_Y, ~adder_1_out[0], adder_1_out[1]);  // AND_Gate
  and and_3 (EXIBINDO_CHUTE, adder_1_out[0], adder_1_out[1]);
  and and_4 (GERAR, ~adder_1_out[0], ~adder_1_out[1]);  // AND_Gate
  Counter #(.width(1), .max('h1)) counter_1 (.count(1'b1), .Q(JOGADOR), .clk(CHUTANDO_X));  // open: load, D, carry, clr
endmodule

module TRECO_NUMERODOIS (
  input  I3,
  input  I2,
  input  I1,
  input  I0,
  output E3,
  output E2,
  output E1,
  output E0,
  output SINAL
);

  wire and_1_out, and_2_out, and_3_out, and_4_out, and_5_out, and_6_out, and_7_out, not_1_out, not_2_out,
       not_3_out, not_4_out, not_5_out, not_6_out, not_7_out, not_8_out, not_9_out, not_10_out, not_11_out;

  not not_1 (not_1_out, I2);
  not not_2 (not_2_out, I1);
  not not_3 (not_3_out, I0);
  not not_4 (not_4_out, I3);
  and and_1 (and_1_out, not_4_out, I2);
  not not_5 (not_5_out, I1);
  and and_2 (and_2_out, I2, not_5_out, not_6_out);
  not not_6 (not_6_out, I0);
  and and_3 (and_3_out, I3, not_7_out, I0);
  not not_7 (not_7_out, I2);
  not not_8 (not_8_out, I2);
  and and_4 (and_4_out, I3, not_8_out, I1);
  not not_9 (not_9_out, I3);
  and and_5 (and_5_out, not_9_out, I1);
  and and_6 (and_6_out, I1, not_10_out);
  not not_10 (not_10_out, I0);
  not not_11 (not_11_out, I1);
  and and_7 (and_7_out, I3, not_11_out, I0);
  and and_8 (E3, I3, not_1_out, not_2_out, not_3_out);
  or or_1 (E2, and_1_out, and_2_out, and_3_out, and_4_out);
  or or_2 (E1, and_5_out, and_6_out, and_7_out);

  assign E0 = I0;
  assign SINAL = I3;
endmodule
